# Fritzing sketch Fig.3(a)  board (saved by Fritzing 0.9.3b)
breadboards: 1

parts:
  Part1 = Arduino Nano (Rev3.0) (ICSP)
  hc-sr1 = hc-sr04
  R1 = Resistor [tolerance=±5% resistance=220 package="0805 [SMD]"]
  LED1 = LED - 5mm [color="Red (633nm)" package="5 mm [THT]"]

nets:
  GND: Part1.GND, hc-sr1.GND, LED1.cathode
  N1: Part1.D6, R1.Pin_0
  N2: Part1.D11/MOSI, hc-sr1.Echo
  N3: Part1.D12/MISO, hc-sr1.Trig
  5V: Part1.5V, hc-sr1.VCC
  N4: R1.Pin_1, LED1.anode
